# Fritzing sketch moisture_shield (saved by Fritzing 0.9.3b)
circuit board: 6.88566cm x 5.36311cm
breadboards: 1

parts:
  arduino = Arduino Uno (Rev3)
  JP1 = Header 3 [package=molex-1x3_lock]
  JP3 = Header 3 [package=molex-1x3_lock]
  JP4 = Header 3 [package=molex-1x3_lock]
  JP5 = Header 3 [package=molex-1x3_lock]
  JP6 = Header 3 [package=molex-1x3_lock]
  JP2 = Header 3 [package=molex-1x3_lock]
  Q1 = NPN-Transistor [package="TO92 [THT]"]
  Q2 = NPN-Transistor [package="TO92 [THT]"]
  Q3 = NPN-Transistor [package="TO92 [THT]"]
  Q4 = NPN-Transistor [package="TO92 [THT]"]
  Q5 = NPN-Transistor [package="TO92 [THT]"]
  Q6 = NPN-Transistor [package="TO92 [THT]"]

nets:
  N1: arduino.A0, JP1.3
  N2: arduino.A1, JP2.3
  N3: arduino.A2, JP3.3
  N4: arduino.A3, JP4.3
  N5: arduino.A4/SDA, JP5.3
  N6: arduino.A5/SCL, JP6.3
  N7: arduino.GND, JP1.2, JP3.2, JP4.2, JP5.2, JP6.2, JP2.2
  N8: arduino.D2, Q1.B
  N9: arduino.D3_PWM, Q2.B
  N10: arduino.D4, Q3.B
  N11: arduino.D5_PWM, Q4.B
  N12: arduino.D6_PWM, Q5.B
  N13: arduino.D7, Q6.B
  N14: arduino.5V, Q1.C, Q2.C, Q3.C, Q4.C, Q5.C, Q6.C
  N15: JP1.1, Q1.E
  N16: JP3.1, Q3.E
  N17: JP4.1, Q4.E
  N18: JP5.1, Q5.E
  N19: JP6.1, Q6.E
  N20: JP2.1, Q2.E

notes:
  soil v0.1
